# Fritzing sketch CO2_MIDI_Breadboard (saved by Fritzing 0.9.3b)

parts:
  WeMos_D1_Mini1 = WeMos D1 Mini
  Part1 = SCD30 CO2 Sensor [part_number=SPX-14751 package=scd30]

nets:
  5V: WeMos_D1_Mini1.5V, Part1.VDD
  N1: WeMos_D1_Mini1.D1, Part1.TX/SCL
  N2: WeMos_D1_Mini1.D2, Part1.RX/SDA
  N3: WeMos_D1_Mini1.G, Part1.GND

custom parts:
  SCD30 CO2 Sensor: SCD30 CO2 Sensor Module Sensirion's SCD30 sensor module for HVAC and indoor air quality applications Spark Fun Electronics SKU : SPX-14751
